# Fritzing sketch LD2420 (saved by Fritzing 0.9.10b)
circuit board: 3.38241cm x 3.88484cm
breadboards: 1

parts:
  J1 = female pin header, 5 pins [form="♀ (female)"]
  J2 = double row female pin header, 20 pins [form="♀ (female)"]
  J3 = double row female pin header, 20 pins [form="♀ (female)"]

nets:
  N1: J1.pin1, J2.pin13
  N2: J1.pin2, J2.pin1, J3.pin7, J3.pin20
  N3: J1.pin3, J2.pin15
  N4: J1.pin4, J2.pin16
  N5: J1.pin5, J2.pin17
